# Fritzing sketch habit_tracker (saved by Fritzing 0.9.4)

parts:
  Part1 = Arduino Nano (Rev3.0)
  LED1 = smd LED [color="Red (633nm)" package="0805 [SMD]"]
  LED2 = smd LED [color="Red (633nm)" package="0805 [SMD]"]
  LED3 = smd LED [color="Green (555nm)" package="0805 [SMD]"]
  LED4 = smd LED [color="Green (555nm)" package="0805 [SMD]"]
  VCC1 = Battery block 9V
  S1 = Toggle Switch [package=THT]
  S2 = Toggle Switch [package=THT]
  R1 = Resistor [tolerance=±5% resistance=1k package=THT]
  R2 = Resistor [tolerance=±5% resistance=1k package=THT]
  R3 = Resistor [tolerance=±5% resistance=1k package=THT]
  R4 = Resistor [tolerance=±5% resistance=1k package=THT]

nets:
  N1: Part1.GND, VCC1.-, S1.COM, S2.COM, R1.Pin_0, R2.Pin_1, R3.Pin_0, R4.Pin_1
  N2: Part1.D2, LED1.cathode
  N3: Part1.D3, LED3.cathode
  N4: Part1.D4, S1.L1
  N5: Part1.D5, LED4.cathode
  N6: Part1.D6, LED2.cathode
  N7: Part1.D7, S2.L1
  N8: Part1.VIN, VCC1.+
  N9: LED1.anode, R1.Pin_1
  N10: LED2.anode, R3.Pin_1
  N11: LED3.anode, R2.Pin_0
  N12: LED4.anode, R4.Pin_0
